// Logisim project orange_level_ddco_2.circ as structural Verilog: 1 circuit, main circuit main
module main (
);

  wire clock_1_out, clock_2_out;
  wire [7:0] ram_1_dout, random_1_out;
  wire [15:0] counter_1_q;

  Clock #(.highDuration(2)) clock_1 (.out(clock_1_out));
  Counter #(.max('hffff), .width(16)) counter_1 (
    .clr(1'b0), .count(1'b1), .clk(clock_1_out), .Q(counter_1_q));  // open: load, up, D, carry
  Random random_1 (.clr(1'b0), .next(1'b1), .clk(clock_1_out), .out(random_1_out));
  Clock clock_2 (.out(clock_2_out));
  RAM #(.addrWidth(16)) ram_1 (
    .addr(counter_1_q), .we(1'b1), .clk(clock_2_out), .din(random_1_out), .dout(ram_1_dout));  // open: oe
  Hex_Digit_Display hex_digit_display_1 (.value(ram_1_dout[3:0]));  // open: dp
  Hex_Digit_Display hex_digit_display_2 (.value(ram_1_dout[7:4]));  // open: dp
endmodule
